// Logisim project TTL-Computer.circ as structural Verilog
module Program_Counter (
);

  // _74191 74191_1: pin names not known
  // _74191 74191_2: pin names not known
  // _74191 74191_3: pin names not known
  // _74191 74191_4: pin names not known
endmodule
